// Digital circuit ALU_CU.dig as structural Verilog
module ALU_CU (
  input  BGN,
  input  RST,
  input  CLK,
  input  CNT7,
  input  Q_0,
  input  Q__1,
  input  A_7,
  input  [1:0] OP,
  output c0,
  output c0_2,
  output c1,
  output c2,
  output c3,
  output c4,
  output cR,
  output cL,
  output c5
);

  wire and_1_out, and_2_out, and_3_out, and_4_out, and_5_out, and_6_out, and_7_out, and_8_out, and_9_out,
       and_10_out, and_11_out, rs_ff_1_q, rs_ff_2_q, rs_ff_3_p1, \sequncecntmod_1_φ0 , \sequncecntmod_1_φ1 ,
       \sequncecntmod_1_φ2 , \sequncecntmod_1_φ3 , xor_1_out;

  RS_FF rs_ff_1 (.R(and_1_out), .S(BGN), .Q(rs_ff_1_q));  // open: nQ
  RS_FF rs_ff_2 (.S(and_1_out), .Q(rs_ff_2_q));  // open: R, nQ
  // RS_FF rs_ff_3: pin names not known; wires that end beside it: rs_ff_3_p1
  and and_1 (and_1_out, \sequncecntmod_1_φ3 , rs_ff_1_q);
  sequnceCNTmod sequncecntmod_1 (
    .CLK(CLK), .BGN(BGN), .RST(RST), .\Φ0 (\sequncecntmod_1_φ0 ), .\Φ1 (\sequncecntmod_1_φ1 ),
    .\Φ2 (\sequncecntmod_1_φ2 ), .\Φ3 (\sequncecntmod_1_φ3 ));  // open: END, Φ4, Φ5, Φ6, Φ7
  and and_2 (and_2_out, ~OP[0], OP[1]);  // And
  xor xor_1 (xor_1_out, Q_0, Q__1);
  and and_3 (and_3_out, OP[0], OP[1]);
  and and_4 (and_4_out, ~OP[0], ~OP[1]);  // And
  and and_5 (and_5_out, and_2_out, xor_1_out, \sequncecntmod_1_φ0 , rs_ff_2_q);
  and and_6 (and_6_out, rs_ff_2_q, and_3_out, \sequncecntmod_1_φ3 , A_7);
  and and_7 (and_7_out, A_7, rs_ff_3_p1, and_3_out, \sequncecntmod_1_φ0 );
  and and_8 (and_8_out, rs_ff_2_q, \sequncecntmod_1_φ1 , and_3_out);
  and and_9 (and_9_out, c3, and_2_out, Q_0, ~Q__1);  // And
  and and_10 (and_10_out, c3, \sequncecntmod_1_φ1 , and_3_out);
  and and_11 (and_11_out, OP[1], ~OP[0]);  // And
  and and_12 (c0, and_2_out, \sequncecntmod_1_φ0 , rs_ff_1_q);
  and and_13 (c0_2, \sequncecntmod_1_φ0 , and_3_out, rs_ff_1_q);
  and and_14 (c1, rs_ff_1_q, \sequncecntmod_1_φ1 );
  and and_15 (c2, rs_ff_1_q, \sequncecntmod_1_φ2 );
  or or_1 (c3, and_4_out, and_11_out, and_5_out, and_6_out, and_7_out, and_8_out);
  or or_2 (c4, and_11_out, and_9_out, and_10_out);
  and and_16 (cR, and_2_out, rs_ff_2_q, ~CNT7, \sequncecntmod_1_φ1 );  // And
  and and_17 (cL, and_3_out, \sequncecntmod_1_φ0 , rs_ff_2_q);
  and and_18 (c5, and_3_out, \sequncecntmod_1_φ2 , rs_ff_2_q);
endmodule
